// Logisim project CPU 16 Instrucciones.circ as structural Verilog: 4 circuits, main circuit main
module main (
);

  wire and_1_out, and_2_out, BB, BEQ, bit_extender_2_out, CLEAR, clock_1_out, CMP, comparator_1_eq,
       comparator_1_gt, decoder_1_out0, decoder_1_out1, decoder_1_out2, decoder_1_out3, decoder_1_out4,
       decoder_1_out6, decoder_1_out7, decoder_1_out8, decoder_1_out9, decoder_1_out10, decoder_1_out11,
       decoder_1_out12, decoder_1_out13, decoder_1_out14, decoder_1_out15, Load_2_q, Load_q, nor_1_out,
       not_1_out, not_2_out, or_2_out, or_3_out, or_4_out, register_1_q, register_2_q, register_3_q,
       register_7_q, Store_2_q, Store_q;
  wire [1:0] bit_extender_3_out;
  wire [2:0] cod_1_out_7;
  wire [3:0] alu_1_out_4, controlled_buffer_1_out, controlled_buffer_2_out, controlled_buffer_3_out,
       controlled_buffer_4_out, DATAIN_2_q, DATAIN_3_q, DATAIN_q, MDEST_2_q, MDEST_q, multiplexer_1_out,
       multiplexer_2_out, multiplexer_3_out, RDEST_2_q, RDEST_3_q, RDEST_q, register_6_q, REGISTROS_data_out,
       shifter_1_out;
  wire [7:0] bit_extender_1_out, counter_1_q, register_4_q;
  wire [15:0] register_5_q, rom_1_data;

  or or_1 (CLEAR, and_2_out, register_3_q, and_1_out);
  Counter counter_1 (
    .load(CLEAR), .D(register_4_q), .Q(counter_1_q), .clk(clock_1_out));  // open: count, carry, clr, preset, down
  Clock clock_1 (.out(clock_1_out));
  and and_1 (and_1_out, BEQ, register_1_q);
  and and_2 (and_2_out, BB, register_2_q);
  Register #(.width(1), .Select("low")) register_1 (
    .D(decoder_1_out8), .Q(register_1_q), .clk(clock_1_out), .clr(register_3_q));  // open: en
  ROM #(.dataWidth(16), .Select("low")) rom_1 (.addr(counter_1_q), .data(rom_1_data));
  Register #(.width(1), .Select("low")) register_2 (
    .D(decoder_1_out7), .Q(register_2_q), .clk(clock_1_out), .clr(register_3_q));  // open: en
  Register #(.width(1), .Select("low")) register_3 (
    .D(decoder_1_out6), .Q(register_3_q), .clk(clock_1_out), .clr(and_1_out));  // open: en
  Register #(.Select("low")) register_4 (.D(bit_extender_1_out), .Q(register_4_q), .clk(clock_1_out));  // open: en, clr
  Register #(.width(16), .Select("low")) register_5 (
    .D(rom_1_data), .Q(register_5_q), .clk(clock_1_out));  // open: en, clr
  assign bit_extender_1_out = {{4{1'b0}}, controlled_buffer_1_out};  // Bit_Extender bit_extender_1
  REGISTROS REGISTROS (
    .LOAD(Load_2_q), .DATA_IN(multiplexer_2_out), .RDEST(RDEST_3_q), .RLECTURA(controlled_buffer_3_out),
    .CLK(clock_1_out), .DATA_OUT(REGISTROS_data_out));
  Decoder #(.select(4), .enable("false")) decoder_1 (
    .out0(decoder_1_out0), .out1(decoder_1_out1), .out2(decoder_1_out2), .out3(decoder_1_out3),
    .out4(decoder_1_out4), .out5(CMP), .out6(decoder_1_out6), .out7(decoder_1_out7), .out8(decoder_1_out8),
    .out9(decoder_1_out9), .out10(decoder_1_out10), .out11(decoder_1_out11), .out12(decoder_1_out12),
    .out13(decoder_1_out13), .out14(decoder_1_out14), .out15(decoder_1_out15), .sel(register_5_q[15:12]));
  not not_1 (not_1_out, decoder_1_out0);
  assign controlled_buffer_1_out = not_1_out ? register_5_q[3:0] : 4'bz;  // Controlled_Buffer controlled_buffer_1
  assign controlled_buffer_2_out = not_1_out ? register_5_q[7:4] : 4'bz;  // Controlled_Buffer controlled_buffer_2
  assign controlled_buffer_3_out = not_1_out ? register_5_q[11:8] : 4'bz;  // Controlled_Buffer controlled_buffer_3
  Register #(.width(4), .Select("low")) register_6 (
    .D(controlled_buffer_2_out), .en(decoder_1_out15), .Q(register_6_q), .clk(clock_1_out));  // open: clr
  Bit_Extender #(.in_width(4), .out_width(1), .\type ("zero")) bit_extender_2 (
    .in(register_6_q), .out(bit_extender_2_out));
  or or_2 (or_2_out, decoder_1_out1, decoder_1_out3);
  nor nor_1 (nor_1_out, decoder_1_out3, decoder_1_out4, decoder_1_out15);
  Multiplexer #(.width(4), .enable("false")) multiplexer_1 (
    .in0(controlled_buffer_2_out), .in1(REGISTROS_data_out), .out(multiplexer_1_out), .sel(nor_1_out));
  Shifter #(.width(4)) shifter_1 (.in(REGISTROS_data_out), .\dist (bit_extender_3_out), .out(shifter_1_out));
  Bit_Extender #(.in_width(4), .out_width(2), .\type ("zero")) bit_extender_3 (
    .in(register_6_q), .out(bit_extender_3_out));
  Multiplexer #(.width(4), .enable("false")) multiplexer_2 (
    .in0(multiplexer_3_out), .in1(shifter_1_out), .out(multiplexer_2_out), .sel(bit_extender_2_out));
  Register #(.width(1), .Select("low")) Load (.D(or_2_out), .Q(Load_q), .clk(clock_1_out), .clr(CLEAR));  // open: en
  or or_3 (or_3_out, decoder_1_out2, decoder_1_out4);
  Register #(.width(1), .Select("low")) Store (.D(or_3_out), .Q(Store_q), .clk(clock_1_out), .clr(CLEAR));  // open: en
  Register #(.width(4), .Select("low")) DATAIN (
    .D(multiplexer_1_out), .Q(DATAIN_q), .clk(clock_1_out), .clr(CLEAR));  // open: en
  Register #(.width(4), .Select("low")) RDEST (
    .D(controlled_buffer_3_out), .Q(RDEST_q), .clk(clock_1_out), .clr(CLEAR));  // open: en
  Register #(.width(4), .Select("low")) MDEST (
    .D(controlled_buffer_1_out), .Q(MDEST_q), .clk(clock_1_out), .clr(CLEAR));  // open: en
  Comparator #(.width(4), .mode("unsigned")) comparator_1 (
    .a(DATAIN_q), .b(RDEST_q), .gt(comparator_1_gt), .eq(comparator_1_eq));  // open: lt
  Register #(.width(1), .Select("low")) u_BB (
    .D(comparator_1_gt), .en(register_7_q), .Q(BB), .clk(clock_1_out));  // open: clr
  Register #(.width(1), .Select("low")) register_7 (.D(CMP), .Q(register_7_q), .clk(clock_1_out));  // open: en, clr
  or or_4 (or_4_out, decoder_1_out14, decoder_1_out13, decoder_1_out10, decoder_1_out9, decoder_1_out11);
  alu alu_1 (.in_1(DATAIN_q), .in_2(RDEST_q), .in_3(cod_1_out_7), .out_4(alu_1_out_4));
  cod cod_1 (
    .in_1(decoder_1_out14), .in_2(decoder_1_out13), .in_3(decoder_1_out12), .in_4(decoder_1_out11),
    .in_5(decoder_1_out10), .in_6(decoder_1_out9), .out_7(cod_1_out_7));
  Register #(.width(1), .Select("low")) u_BEQ (
    .D(comparator_1_eq), .en(register_7_q), .Q(BEQ), .clk(clock_1_out));  // open: clr
  Register #(.width(1), .Select("low")) Store_2 (
    .D(Store_q), .Q(Store_2_q), .clk(clock_1_out), .clr(CLEAR));  // open: en
  Register #(.width(4), .Select("low")) DATAIN_2 (
    .D(DATAIN_q), .Q(DATAIN_2_q), .clk(clock_1_out), .clr(CLEAR));  // open: en
  Register #(.width(4), .Select("low")) RDEST_2 (
    .D(RDEST_q), .Q(RDEST_2_q), .clk(clock_1_out), .clr(CLEAR));  // open: en
  Register #(.width(4), .Select("low")) MDEST_2 (
    .D(MDEST_q), .Q(MDEST_2_q), .clk(clock_1_out), .clr(CLEAR));  // open: en
  assign controlled_buffer_4_out = Store_2_q ? DATAIN_2_q : 4'bz;  // Controlled_Buffer controlled_buffer_4
  not not_2 (not_2_out, Store_2_q);
  RAM #(.addrWidth(4), .dataWidth(4), .Select("low")) ram_1 (
    .addr(MDEST_2_q), .data(controlled_buffer_4_out), .clk(clock_1_out), .ld(not_2_out));  // open: sel, clr
  Register #(.width(1), .Select("low")) Load_2 (.D(Load_q), .Q(Load_2_q), .clk(clock_1_out));  // open: en, clr
  Register #(.width(4), .Select("low")) DATAIN_3 (
    .D(controlled_buffer_4_out), .Q(DATAIN_3_q), .clk(clock_1_out));  // open: en, clr
  Register #(.width(4), .Select("low")) RDEST_3 (.D(RDEST_2_q), .Q(RDEST_3_q), .clk(clock_1_out));  // open: en, clr
  Multiplexer #(.width(4), .enable("false")) multiplexer_3 (
    .in0(DATAIN_3_q), .in1(alu_1_out_4), .out(multiplexer_3_out), .sel(or_4_out));

  // Notes on the sheet:
  //   Andrés, Orlando, Selassie
  //   IF
  //   contents of rom_1 (hex, n*v repeats v):
  //   4041 0 4022 0 1101 0 1202 0 e124 0 9126 789 600f 4022 0 a127 0 b128 0 c129 0 f120 0 5120 7000 30*0
  //   6000
  //   DEC
  //   MEM
  //   WB
endmodule

module REGISTROS (
  input  LOAD,
  input  [3:0] DATA_IN,
  input  [3:0] RDEST,
  input  [3:0] RLECTURA,
  input  CLK,
  output [3:0] DATA_OUT
);

  wire and_1_out, and_2_out, and_3_out, and_4_out, and_5_out, and_6_out, and_7_out, and_8_out, and_9_out,
       and_10_out, and_11_out, and_12_out, and_13_out, and_14_out, and_15_out, and_16_out, decoder_1_out0,
       decoder_1_out1, decoder_1_out2, decoder_1_out3, decoder_1_out4, decoder_1_out5, decoder_1_out6,
       decoder_1_out7, decoder_1_out8, decoder_1_out9, decoder_1_out10, decoder_1_out11, decoder_1_out12,
       decoder_1_out13, decoder_1_out14, decoder_1_out15;
  wire [3:0] register_1_q, register_2_q, register_3_q, register_4_q, register_5_q, register_6_q,
       register_7_q, register_8_q, register_9_q, register_10_q, register_11_q, register_12_q, register_13_q,
       register_14_q, register_15_q, register_16_q;

  Decoder #(.select(4), .enable("false")) decoder_1 (
    .out0(decoder_1_out0), .out1(decoder_1_out1), .out2(decoder_1_out2), .out3(decoder_1_out3),
    .out4(decoder_1_out4), .out5(decoder_1_out5), .out6(decoder_1_out6), .out7(decoder_1_out7),
    .out8(decoder_1_out8), .out9(decoder_1_out9), .out10(decoder_1_out10), .out11(decoder_1_out11),
    .out12(decoder_1_out12), .out13(decoder_1_out13), .out14(decoder_1_out14), .out15(decoder_1_out15),
    .sel(RDEST));
  Register #(.width(4), .Select("low")) register_1 (
    .D(DATA_IN), .en(and_1_out), .Q(register_1_q), .clk(CLK));  // open: clr
  and and_1 (and_1_out, LOAD, decoder_1_out0);
  and and_2 (and_2_out, LOAD, decoder_1_out1);
  Register #(.width(4), .Select("low")) register_2 (
    .D(DATA_IN), .en(and_2_out), .Q(register_2_q), .clk(CLK));  // open: clr
  and and_3 (and_3_out, LOAD, decoder_1_out2);
  Register #(.width(4), .Select("low")) register_3 (
    .D(DATA_IN), .en(and_3_out), .Q(register_3_q), .clk(CLK));  // open: clr
  and and_4 (and_4_out, LOAD, decoder_1_out3);
  Register #(.width(4), .Select("low")) register_4 (
    .D(DATA_IN), .en(and_4_out), .Q(register_4_q), .clk(CLK));  // open: clr
  and and_5 (and_5_out, LOAD, decoder_1_out4);
  and and_6 (and_6_out, LOAD, decoder_1_out5);
  and and_7 (and_7_out, LOAD, decoder_1_out6);
  and and_8 (and_8_out, LOAD, decoder_1_out7);
  Register #(.width(4), .Select("low")) register_5 (
    .D(DATA_IN), .en(and_5_out), .Q(register_5_q), .clk(CLK));  // open: clr
  Register #(.width(4), .Select("low")) register_6 (
    .D(DATA_IN), .en(and_6_out), .Q(register_6_q), .clk(CLK));  // open: clr
  Register #(.width(4), .Select("low")) register_7 (
    .D(DATA_IN), .en(and_7_out), .Q(register_7_q), .clk(CLK));  // open: clr
  Register #(.width(4), .Select("low")) register_8 (
    .D(DATA_IN), .en(and_8_out), .Q(register_8_q), .clk(CLK));  // open: clr
  Multiplexer #(.select(4), .width(4), .enable("false")) multiplexer_1 (
    .in0(register_1_q), .in1(register_2_q), .in2(register_3_q), .in3(register_4_q), .in4(register_5_q),
    .in5(register_6_q), .in6(register_7_q), .in7(register_8_q), .in8(register_9_q), .in9(register_10_q),
    .in10(register_11_q), .in11(register_12_q), .in12(register_13_q), .in13(register_14_q),
    .in14(register_15_q), .in15(register_16_q), .out(DATA_OUT), .sel(RLECTURA));
  and and_9 (and_9_out, LOAD, decoder_1_out8);
  and and_10 (and_10_out, LOAD, decoder_1_out9);
  and and_11 (and_11_out, LOAD, decoder_1_out10);
  and and_12 (and_12_out, LOAD, decoder_1_out11);
  Register #(.width(4), .Select("low")) register_9 (
    .D(DATA_IN), .en(and_9_out), .Q(register_9_q), .clk(CLK));  // open: clr
  Register #(.width(4), .Select("low")) register_10 (
    .D(DATA_IN), .en(and_10_out), .Q(register_10_q), .clk(CLK));  // open: clr
  Register #(.width(4), .Select("low")) register_11 (
    .D(DATA_IN), .en(and_11_out), .Q(register_11_q), .clk(CLK));  // open: clr
  Register #(.width(4), .Select("low")) register_12 (
    .D(DATA_IN), .en(and_12_out), .Q(register_12_q), .clk(CLK));  // open: clr
  and and_13 (and_13_out, LOAD, decoder_1_out12);
  and and_14 (and_14_out, LOAD, decoder_1_out13);
  and and_15 (and_15_out, LOAD, decoder_1_out14);
  and and_16 (and_16_out, LOAD, decoder_1_out15);
  Register #(.width(4), .Select("low")) register_13 (
    .D(DATA_IN), .en(and_13_out), .Q(register_13_q), .clk(CLK));  // open: clr
  Register #(.width(4), .Select("low")) register_14 (
    .D(DATA_IN), .en(and_14_out), .Q(register_14_q), .clk(CLK));  // open: clr
  Register #(.width(4), .Select("low")) register_15 (
    .D(DATA_IN), .en(and_15_out), .Q(register_15_q), .clk(CLK));  // open: clr
  Register #(.width(4), .Select("low")) register_16 (
    .D(DATA_IN), .en(and_16_out), .Q(register_16_q), .clk(CLK));  // open: clr
endmodule

module alu (
  input  [3:0] in_1,
  input  [3:0] in_2,
  input  [2:0] in_3,
  output [3:0] out_4
);

  wire [3:0] adder_1_out, and_1_out, not_1_out, or_1_out, subtractor_1_out, xor_1_out;

  assign not_1_out = ~in_1;  // NOT_Gate not_1, 4 bits wide
  assign and_1_out = in_1 & in_2;  // AND_Gate and_1, 4 bits wide
  assign or_1_out = in_1 | in_2;  // OR_Gate or_1, 4 bits wide
  assign xor_1_out = in_1 ^ in_2;  // XOR_Gate xor_1, 4 bits wide
  Adder #(.width(4)) adder_1 (.a(in_1), .b(in_2), .out(adder_1_out));  // open: cin, cout
  Subtractor #(.width(4)) subtractor_1 (.a(in_1), .b(in_2), .out(subtractor_1_out));  // open: bin, bout
  Multiplexer #(.select(3), .width(4), .enable("false")) multiplexer_1 (
    .in0(and_1_out), .in1(or_1_out), .in2(xor_1_out), .in3(not_1_out), .in4(adder_1_out),
    .in5(subtractor_1_out), .out(out_4), .sel(in_3));  // open: in6, in7
endmodule

module cod (
  input  in_1,
  input  in_2,
  input  in_3,
  input  in_4,
  input  in_5,
  input  in_6,
  output [2:0] out_7
);

  or or_1 (out_7[2], in_3, in_4, in_5, in_6);
  or or_2 (out_7[1], in_6, in_2, in_1, in_5);
  or or_3 (out_7[0], in_6, in_4, in_2);
endmodule
